# Fritzing sketch Arduino4Bio-EnviroDataLogger (saved by Fritzing 0.8.7b)
circuit board: 8.46667cm x 5.64444cm
breadboards: 1

parts:
  Part1 = Arduino Ethernet Shield (Rev3)
  RHT1 = Humidity and Temperature Sensor RHT03

nets:
  N1: Part1.GND, RHT1.GND_2
  N2: Part1.D2, RHT1.Data-signal
  5V: Part1.5V, RHT1.Vcc
